// Logisim project IOC_TRABALHO_PRATICO_2.circ as structural Verilog: 16 circuits, main circuit main
module main (
);

  ALU alu_1 ();  // open: A, B, C, A7, A6, A5, A4, A3, A2, A1, A0, B7, B6, B5, B4, B3, B2, B1, B0, Adapter16Bits, S7, S6, S5, S4, S3, S2, S1, S0, Carry, Z
endmodule

module FullAdder (
  input  isActive,
  input  Cinp,
  input  Ai,
  input  Bi,
  output Si,
  output Cout
);

  wire and_1_out, and_2_out, key_1_s, key_2_s, key_3_s, or_1_out, xor_1_out;

  Key key_1 (.ACTIVE(isActive), .A(Ai), .S(key_1_s));
  Key key_2 (.ACTIVE(isActive), .A(Bi), .S(key_2_s));
  and and_1 (and_1_out, key_2_s, key_1_s);
  Key key_3 (.ACTIVE(isActive), .A(Cinp), .S(key_3_s));
  or or_1 (or_1_out, key_2_s, key_1_s);
  and and_2 (and_2_out, key_3_s, or_1_out);
  or or_2 (Cout, and_1_out, and_2_out);
  xor xor_1 (xor_1_out, key_1_s, key_2_s);
  xor xor_2 (Si, key_3_s, xor_1_out);
endmodule

module EightBitsAdder (
  input  isActive,
  input  A0,
  input  B0,
  input  A1,
  input  B1,
  input  A2,
  input  B2,
  input  A3,
  input  B3,
  input  A4,
  input  B4,
  input  A5,
  input  B5,
  input  A6,
  input  B6,
  input  A7,
  input  B7,
  input  CarryIn,
  output S0,
  output S1,
  output S2,
  output S3,
  output S4,
  output S5,
  output S6,
  output S7,
  output LastCarry
);

  wire fulladder_1_cout, fulladder_2_cout, fulladder_3_cout, fulladder_4_cout, fulladder_5_cout,
       fulladder_6_cout, fulladder_7_cout;

  FullAdder fulladder_1 (.isActive(isActive), .Cinp(CarryIn), .Ai(A0), .Bi(B0), .Si(S0), .Cout(fulladder_1_cout));
  FullAdder fulladder_2 (
    .isActive(isActive), .Cinp(fulladder_1_cout), .Ai(A1), .Bi(B1), .Si(S1), .Cout(fulladder_2_cout));
  FullAdder fulladder_3 (
    .isActive(isActive), .Cinp(fulladder_2_cout), .Ai(A2), .Bi(B2), .Si(S2), .Cout(fulladder_3_cout));
  FullAdder fulladder_4 (
    .isActive(isActive), .Cinp(fulladder_3_cout), .Ai(A3), .Bi(B3), .Si(S3), .Cout(fulladder_4_cout));
  FullAdder fulladder_5 (
    .isActive(isActive), .Cinp(fulladder_4_cout), .Ai(A4), .Bi(B4), .Si(S4), .Cout(fulladder_5_cout));
  FullAdder fulladder_6 (
    .isActive(isActive), .Cinp(fulladder_5_cout), .Ai(A5), .Bi(B5), .Si(S5), .Cout(fulladder_6_cout));
  FullAdder fulladder_7 (
    .isActive(isActive), .Cinp(fulladder_6_cout), .Ai(A6), .Bi(B6), .Si(S6), .Cout(fulladder_7_cout));
  FullAdder fulladder_8 (.isActive(isActive), .Cinp(fulladder_7_cout), .Ai(A7), .Bi(B7), .Si(S7), .Cout(LastCarry));
endmodule

module FullSubtrator (
  input  isActive,
  input  Binp,
  input  A,
  input  B,
  output S,
  output Bout
);

  wire and_1_out, and_2_out, key_1_s, key_2_s, key_3_s, not_1_out, not_2_out, xor_1_out;

  Key key_1 (.ACTIVE(isActive), .A(A), .S(key_1_s));
  Key key_2 (.ACTIVE(isActive), .A(B), .S(key_2_s));
  not not_1 (not_1_out, key_1_s);
  xor xor_1 (xor_1_out, key_1_s, key_2_s);
  Key key_3 (.ACTIVE(isActive), .A(Binp), .S(key_3_s));
  not not_2 (not_2_out, xor_1_out);
  and and_1 (and_1_out, key_2_s, not_1_out);
  and and_2 (and_2_out, not_2_out, key_3_s);
  xor xor_2 (S, key_3_s, xor_1_out);
  or or_1 (Bout, and_2_out, and_1_out);
endmodule

module EightBitsSubtrator (
  input  isActive,
  input  A0,
  input  B0,
  input  A1,
  input  B1,
  input  A2,
  input  B2,
  input  A3,
  input  B3,
  input  A4,
  input  B4,
  input  A5,
  input  B5,
  input  A6,
  input  B6,
  input  A7,
  input  B7,
  input  BorrowIN,
  output S0,
  output S1,
  output S2,
  output S3,
  output S4,
  output S5,
  output S6,
  output S7,
  output LastBorrow
);

  wire fullsubtrator_1_bout, fullsubtrator_2_bout, fullsubtrator_3_bout, fullsubtrator_4_bout,
       fullsubtrator_5_bout, fullsubtrator_6_bout, fullsubtrator_7_bout;

  FullSubtrator fullsubtrator_1 (
    .isActive(isActive), .Binp(BorrowIN), .A(A0), .B(B0), .S(S0), .Bout(fullsubtrator_1_bout));
  FullSubtrator fullsubtrator_2 (
    .isActive(isActive), .Binp(fullsubtrator_1_bout), .A(A1), .B(B1), .S(S1), .Bout(fullsubtrator_2_bout));
  FullSubtrator fullsubtrator_3 (
    .isActive(isActive), .Binp(fullsubtrator_2_bout), .A(A2), .B(B2), .S(S2), .Bout(fullsubtrator_3_bout));
  FullSubtrator fullsubtrator_4 (
    .isActive(isActive), .Binp(fullsubtrator_3_bout), .A(A3), .B(B3), .S(S3), .Bout(fullsubtrator_4_bout));
  FullSubtrator fullsubtrator_5 (
    .isActive(isActive), .Binp(fullsubtrator_4_bout), .A(A4), .B(B4), .S(S4), .Bout(fullsubtrator_5_bout));
  FullSubtrator fullsubtrator_6 (
    .isActive(isActive), .Binp(fullsubtrator_5_bout), .A(A5), .B(B5), .S(S5), .Bout(fullsubtrator_6_bout));
  FullSubtrator fullsubtrator_7 (
    .isActive(isActive), .Binp(fullsubtrator_6_bout), .A(A6), .B(B6), .S(S6), .Bout(fullsubtrator_7_bout));
  FullSubtrator fullsubtrator_8 (
    .isActive(isActive), .Binp(fullsubtrator_7_bout), .A(A7), .B(B7), .S(S7), .Bout(LastBorrow));
endmodule

module OrBitToBit (
  input  isActive,
  input  A0,
  input  B0,
  input  A1,
  input  B1,
  input  A2,
  input  B2,
  input  A3,
  input  B3,
  input  A4,
  input  B4,
  input  A5,
  input  B5,
  input  A6,
  input  B6,
  input  A7,
  input  B7,
  output S0,
  output S1,
  output S2,
  output S3,
  output S4,
  output S5,
  output S6,
  output S7
);

  wire or_1_out, or_2_out, or_3_out, or_4_out, or_5_out, or_6_out, or_7_out, or_8_out;

  or or_1 (or_1_out, A0, B0);
  or or_2 (or_2_out, A1, B1);
  or or_3 (or_3_out, A2, B2);
  or or_4 (or_4_out, A3, B3);
  or or_5 (or_5_out, A4, B4);
  or or_6 (or_6_out, A5, B5);
  or or_7 (or_7_out, A6, B6);
  or or_8 (or_8_out, A7, B7);
  Key key_1 (.ACTIVE(isActive), .A(or_1_out), .S(S0));
  Key key_2 (.ACTIVE(isActive), .A(or_2_out), .S(S1));
  Key key_3 (.ACTIVE(isActive), .A(or_3_out), .S(S2));
  Key key_4 (.ACTIVE(isActive), .A(or_4_out), .S(S3));
  Key key_5 (.ACTIVE(isActive), .A(or_5_out), .S(S4));
  Key key_6 (.ACTIVE(isActive), .A(or_6_out), .S(S5));
  Key key_7 (.ACTIVE(isActive), .A(or_7_out), .S(S6));
  Key key_8 (.ACTIVE(isActive), .A(or_8_out), .S(S7));
endmodule

module AndBitToBit (
  input  isActive,
  input  A0,
  input  B0,
  input  A1,
  input  B1,
  input  A2,
  input  B2,
  input  A3,
  input  B3,
  input  A4,
  input  B4,
  input  A5,
  input  B5,
  input  A6,
  input  B6,
  input  A7,
  input  B7,
  output S0,
  output S1,
  output S2,
  output S3,
  output S4,
  output S5,
  output S6,
  output S7
);

  wire and_1_out, and_2_out, and_3_out, and_4_out, and_5_out, and_6_out, and_7_out, and_8_out;

  and and_1 (and_1_out, A0, B0);
  and and_2 (and_2_out, A1, B1);
  and and_3 (and_3_out, A2, B2);
  and and_4 (and_4_out, A3, B3);
  and and_5 (and_5_out, A4, B4);
  and and_6 (and_6_out, A5, B5);
  and and_7 (and_7_out, A6, B6);
  and and_8 (and_8_out, A7, B7);
  Key key_1 (.ACTIVE(isActive), .A(and_1_out), .S(S0));
  Key key_2 (.ACTIVE(isActive), .A(and_2_out), .S(S1));
  Key key_3 (.ACTIVE(isActive), .A(and_3_out), .S(S2));
  Key key_4 (.ACTIVE(isActive), .A(and_4_out), .S(S3));
  Key key_5 (.ACTIVE(isActive), .A(and_5_out), .S(S4));
  Key key_6 (.ACTIVE(isActive), .A(and_6_out), .S(S5));
  Key key_7 (.ACTIVE(isActive), .A(and_7_out), .S(S6));
  Key key_8 (.ACTIVE(isActive), .A(and_8_out), .S(S7));
endmodule

module XorBitToBit (
  input  isActive,
  input  A0,
  input  B0,
  input  A1,
  input  B1,
  input  A2,
  input  B2,
  input  A3,
  input  B3,
  input  A4,
  input  B4,
  input  A5,
  input  B5,
  input  A6,
  input  B6,
  input  A7,
  input  B7,
  output S0,
  output S1,
  output S2,
  output S3,
  output S4,
  output S5,
  output S6,
  output S7
);

  wire xor_1_out, xor_2_out, xor_3_out, xor_4_out, xor_5_out, xor_6_out, xor_7_out, xor_8_out;

  xor xor_1 (xor_1_out, A0, B0);
  xor xor_2 (xor_2_out, A1, B1);
  xor xor_3 (xor_3_out, A2, B2);
  xor xor_4 (xor_4_out, A3, B3);
  xor xor_5 (xor_5_out, A4, B4);
  xor xor_6 (xor_6_out, A5, B5);
  xor xor_7 (xor_7_out, A6, B6);
  xor xor_8 (xor_8_out, A7, B7);
  Key key_1 (.ACTIVE(isActive), .A(xor_1_out), .S(S0));
  Key key_2 (.ACTIVE(isActive), .A(xor_2_out), .S(S1));
  Key key_3 (.ACTIVE(isActive), .A(xor_3_out), .S(S2));
  Key key_4 (.ACTIVE(isActive), .A(xor_4_out), .S(S3));
  Key key_5 (.ACTIVE(isActive), .A(xor_5_out), .S(S4));
  Key key_6 (.ACTIVE(isActive), .A(xor_6_out), .S(S5));
  Key key_7 (.ACTIVE(isActive), .A(xor_7_out), .S(S6));
  Key key_8 (.ACTIVE(isActive), .A(xor_8_out), .S(S7));
endmodule

module OperationInput (
  input  A,
  input  B,
  input  C,
  output ADD,
  output SUB,
  output XORLogic,
  output ANDLogic,
  output ORLogic,
  output ShiftLeft,
  output ShiftRight,
  output NONE
);

  wire and_1_out, and_2_out, and_3_out, and_4_out, and_5_out, and_6_out, and_7_out, and_8_out, not_1_out,
       not_2_out, not_3_out;

  not not_1 (not_1_out, A);
  not not_2 (not_2_out, B);
  not not_3 (not_3_out, C);
  and and_1 (and_1_out, not_1_out, not_2_out);
  and and_2 (and_2_out, not_1_out, not_2_out);
  and and_3 (and_3_out, not_1_out, B);
  and and_4 (and_4_out, A, not_2_out);
  and and_5 (and_5_out, not_1_out, B);
  and and_6 (and_6_out, A, not_2_out);
  and and_7 (and_7_out, A, B);
  and and_8 (and_8_out, A, B);
  and and_9 (ADD, and_1_out, not_3_out);
  and and_10 (SUB, and_2_out, C);
  and and_11 (XORLogic, and_3_out, not_3_out);
  and and_12 (ANDLogic, and_4_out, not_3_out);
  and and_13 (ORLogic, and_5_out, C);
  and and_14 (ShiftLeft, and_6_out, C);
  and and_15 (ShiftRight, and_7_out, not_3_out);
  and and_16 (NONE, and_8_out, C);
endmodule

module SHLShiftLeft (
  input  isActive,
  input  A0,
  input  A1,
  input  A2,
  input  A3,
  input  A4,
  input  A5,
  input  A6,
  input  A7,
  input  Carry,
  output S0,
  output S1,
  output S2,
  output S3,
  output S4,
  output S5,
  output S6,
  output S7,
  output Discart
);

  Key key_1 (.ACTIVE(isActive), .A(A0), .S(S1));
  Key key_2 (.ACTIVE(isActive), .A(A1), .S(S2));
  Key key_3 (.ACTIVE(isActive), .A(A2), .S(S3));
  Key key_4 (.ACTIVE(isActive), .A(A3), .S(S4));
  Key key_5 (.ACTIVE(isActive), .A(A4), .S(S5));
  Key key_6 (.ACTIVE(isActive), .A(A5), .S(S6));
  Key key_7 (.ACTIVE(isActive), .A(A6), .S(S7));
  Key key_8 (.ACTIVE(isActive), .A(A7), .S(Discart));
  Key key_9 (.ACTIVE(isActive), .A(Carry), .S(S0));
endmodule

module SHLShiftRight (
  input  isActive,
  input  A0,
  input  A1,
  input  A2,
  input  A3,
  input  A4,
  input  A5,
  input  A6,
  input  A7,
  input  Carry,
  output Discart,
  output S0,
  output S1,
  output S2,
  output S3,
  output S4,
  output S5,
  output S6,
  output S7
);

  Key key_1 (.ACTIVE(isActive), .A(A0), .S(Discart));
  Key key_2 (.ACTIVE(isActive), .A(A1), .S(S0));
  Key key_3 (.ACTIVE(isActive), .A(A2), .S(S1));
  Key key_4 (.ACTIVE(isActive), .A(A3), .S(S2));
  Key key_5 (.ACTIVE(isActive), .A(A4), .S(S3));
  Key key_6 (.ACTIVE(isActive), .A(A5), .S(S4));
  Key key_7 (.ACTIVE(isActive), .A(A6), .S(S5));
  Key key_8 (.ACTIVE(isActive), .A(A7), .S(S6));
  Key key_9 (.ACTIVE(isActive), .A(Carry), .S(S7));
endmodule

module ALU (
  input  A,
  input  B,
  input  C,
  input  A7,
  input  A6,
  input  A5,
  input  A4,
  input  A3,
  input  A2,
  input  A1,
  input  A0,
  input  B7,
  input  B6,
  input  B5,
  input  B4,
  input  B3,
  input  B2,
  input  B1,
  input  B0,
  input  Adapter16Bits,
  output S7,
  output S6,
  output S5,
  output S4,
  output S3,
  output S2,
  output S1,
  output S0,
  output Carry,
  output Z
);

  wire andbittobit_1_s0, andbittobit_1_s1, andbittobit_1_s2, andbittobit_1_s3, andbittobit_1_s4,
       andbittobit_1_s5, andbittobit_1_s6, andbittobit_1_s7, eightbitsadder_1_lastcarry, eightbitsadder_1_s0,
       eightbitsadder_1_s1, eightbitsadder_1_s2, eightbitsadder_1_s3, eightbitsadder_1_s4,
       eightbitsadder_1_s5, eightbitsadder_1_s6, eightbitsadder_1_s7, eightbitssubtrator_1_lastborrow,
       eightbitssubtrator_1_s0, eightbitssubtrator_1_s1, eightbitssubtrator_1_s2, eightbitssubtrator_1_s3,
       eightbitssubtrator_1_s4, eightbitssubtrator_1_s5, eightbitssubtrator_1_s6, eightbitssubtrator_1_s7,
       not_1_out, not_2_out, not_3_out, not_4_out, not_5_out, not_6_out, not_7_out, not_8_out,
       operationinput_1_add, operationinput_1_andlogic, operationinput_1_orlogic, operationinput_1_shiftleft,
       operationinput_1_shiftright, operationinput_1_sub, operationinput_1_xorlogic, orbittobit_1_s0,
       orbittobit_1_s1, orbittobit_1_s2, orbittobit_1_s3, orbittobit_1_s4, orbittobit_1_s5, orbittobit_1_s6,
       orbittobit_1_s7, shlshiftleft_1_discart, shlshiftleft_1_s0, shlshiftleft_1_s1, shlshiftleft_1_s2,
       shlshiftleft_1_s3, shlshiftleft_1_s4, shlshiftleft_1_s5, shlshiftleft_1_s6, shlshiftleft_1_s7,
       shlshiftright_1_discart, shlshiftright_1_s0, shlshiftright_1_s1, shlshiftright_1_s2,
       shlshiftright_1_s3, shlshiftright_1_s4, shlshiftright_1_s5, shlshiftright_1_s6, shlshiftright_1_s7,
       xorbittobit_1_s0, xorbittobit_1_s1, xorbittobit_1_s2, xorbittobit_1_s3, xorbittobit_1_s4,
       xorbittobit_1_s5, xorbittobit_1_s6, xorbittobit_1_s7;

  OperationInput operationinput_1 (
    .A(A), .B(B), .C(C), .ADD(operationinput_1_add), .SUB(operationinput_1_sub),
    .XORLogic(operationinput_1_xorlogic), .ANDLogic(operationinput_1_andlogic),
    .ORLogic(operationinput_1_orlogic), .ShiftLeft(operationinput_1_shiftleft),
    .ShiftRight(operationinput_1_shiftright));  // open: NONE
  EightBitsAdder eightbitsadder_1 (
    .isActive(operationinput_1_add), .A0(A0), .B0(B0), .A1(A1), .B1(B1), .A2(A2), .B2(B2), .A3(A3), .B3(B3),
    .A4(A4), .B4(B4), .A5(A5), .B5(B5), .A6(A6), .B6(B6), .A7(A7), .B7(B7), .CarryIn(Adapter16Bits),
    .S0(eightbitsadder_1_s0), .S1(eightbitsadder_1_s1), .S2(eightbitsadder_1_s2), .S3(eightbitsadder_1_s3),
    .S4(eightbitsadder_1_s4), .S5(eightbitsadder_1_s5), .S6(eightbitsadder_1_s6), .S7(eightbitsadder_1_s7),
    .LastCarry(eightbitsadder_1_lastcarry));
  EightBitsSubtrator eightbitssubtrator_1 (
    .isActive(operationinput_1_sub), .A0(A0), .B0(B0), .A1(A1), .B1(B1), .A2(A2), .B2(B2), .A3(A3), .B3(B3),
    .A4(A4), .B4(B4), .A5(A5), .B5(B5), .A6(A6), .B6(B6), .A7(A7), .B7(B7), .BorrowIN(Adapter16Bits),
    .S0(eightbitssubtrator_1_s0), .S1(eightbitssubtrator_1_s1), .S2(eightbitssubtrator_1_s2),
    .S3(eightbitssubtrator_1_s3), .S4(eightbitssubtrator_1_s4), .S5(eightbitssubtrator_1_s5),
    .S6(eightbitssubtrator_1_s6), .S7(eightbitssubtrator_1_s7), .LastBorrow(eightbitssubtrator_1_lastborrow));
  XorBitToBit xorbittobit_1 (
    .isActive(operationinput_1_xorlogic), .A0(A0), .B0(B0), .A1(A1), .B1(B1), .A2(A2), .B2(B2), .A3(A3),
    .B3(B3), .A4(A4), .B4(B4), .A5(A5), .B5(B5), .A6(A6), .B6(B6), .A7(A7), .B7(B7), .S0(xorbittobit_1_s0),
    .S1(xorbittobit_1_s1), .S2(xorbittobit_1_s2), .S3(xorbittobit_1_s3), .S4(xorbittobit_1_s4),
    .S5(xorbittobit_1_s5), .S6(xorbittobit_1_s6), .S7(xorbittobit_1_s7));
  AndBitToBit andbittobit_1 (
    .isActive(operationinput_1_andlogic), .A0(A0), .B0(B0), .A1(A1), .B1(B1), .A2(A2), .B2(B2), .A3(A3),
    .B3(B3), .A4(A4), .B4(B4), .A5(A5), .B5(B5), .A6(A6), .B6(B6), .A7(A7), .B7(B7), .S0(andbittobit_1_s0),
    .S1(andbittobit_1_s1), .S2(andbittobit_1_s2), .S3(andbittobit_1_s3), .S4(andbittobit_1_s4),
    .S5(andbittobit_1_s5), .S6(andbittobit_1_s6), .S7(andbittobit_1_s7));
  OrBitToBit orbittobit_1 (
    .isActive(operationinput_1_orlogic), .A0(A0), .B0(B0), .A1(A1), .B1(B1), .A2(A2), .B2(B2), .A3(A3),
    .B3(B3), .A4(A4), .B4(B4), .A5(A5), .B5(B5), .A6(A6), .B6(B6), .A7(A7), .B7(B7), .S0(orbittobit_1_s0),
    .S1(orbittobit_1_s1), .S2(orbittobit_1_s2), .S3(orbittobit_1_s3), .S4(orbittobit_1_s4),
    .S5(orbittobit_1_s5), .S6(orbittobit_1_s6), .S7(orbittobit_1_s7));
  SHLShiftLeft shlshiftleft_1 (
    .isActive(operationinput_1_shiftleft), .A0(A0), .A1(A1), .A2(A2), .A3(A3), .A4(A4), .A5(A5), .A6(A6),
    .A7(A7), .Carry(Adapter16Bits), .S0(shlshiftleft_1_s0), .S1(shlshiftleft_1_s1), .S2(shlshiftleft_1_s2),
    .S3(shlshiftleft_1_s3), .S4(shlshiftleft_1_s4), .S5(shlshiftleft_1_s5), .S6(shlshiftleft_1_s6),
    .S7(shlshiftleft_1_s7), .Discart(shlshiftleft_1_discart));
  SHLShiftRight shlshiftright_1 (
    .isActive(operationinput_1_shiftright), .A0(A0), .A1(A1), .A2(A2), .A3(A3), .A4(A4), .A5(A5), .A6(A6),
    .A7(A7), .Carry(Adapter16Bits), .Discart(shlshiftright_1_discart), .S0(shlshiftright_1_s0),
    .S1(shlshiftright_1_s1), .S2(shlshiftright_1_s2), .S3(shlshiftright_1_s3), .S4(shlshiftright_1_s4),
    .S5(shlshiftright_1_s5), .S6(shlshiftright_1_s6), .S7(shlshiftright_1_s7));
  or or_1 (S7, eightbitsadder_1_s7, eightbitssubtrator_1_s7, xorbittobit_1_s7, andbittobit_1_s7, orbittobit_1_s7, shlshiftleft_1_s7, shlshiftright_1_s7);
  not not_1 (not_1_out, S7);
  or or_2 (S6, eightbitsadder_1_s6, eightbitssubtrator_1_s6, xorbittobit_1_s6, andbittobit_1_s6, orbittobit_1_s6, shlshiftleft_1_s6, shlshiftright_1_s6);
  not not_2 (not_2_out, S6);
  not not_3 (not_3_out, S5);
  or or_3 (S5, eightbitsadder_1_s5, eightbitssubtrator_1_s5, xorbittobit_1_s5, andbittobit_1_s5, orbittobit_1_s5, shlshiftleft_1_s5, shlshiftright_1_s5);
  or or_4 (S4, eightbitsadder_1_s4, eightbitssubtrator_1_s4, xorbittobit_1_s4, andbittobit_1_s4, orbittobit_1_s4, shlshiftleft_1_s4, shlshiftright_1_s4);
  not not_4 (not_4_out, S4);
  or or_5 (S3, eightbitsadder_1_s3, eightbitssubtrator_1_s3, xorbittobit_1_s3, andbittobit_1_s3, orbittobit_1_s3, shlshiftleft_1_s3, shlshiftright_1_s3);
  not not_5 (not_5_out, S3);
  or or_6 (S2, eightbitsadder_1_s2, eightbitssubtrator_1_s2, xorbittobit_1_s2, andbittobit_1_s2, orbittobit_1_s2, shlshiftleft_1_s2, shlshiftright_1_s2);
  not not_6 (not_6_out, S2);
  or or_7 (S1, eightbitsadder_1_s1, eightbitssubtrator_1_s1, xorbittobit_1_s1, andbittobit_1_s1, orbittobit_1_s1, shlshiftleft_1_s1, shlshiftright_1_s1);
  not not_7 (not_7_out, S1);
  or or_8 (S0, eightbitsadder_1_s0, eightbitssubtrator_1_s0, xorbittobit_1_s0, andbittobit_1_s0, orbittobit_1_s0, shlshiftleft_1_s0, shlshiftright_1_s0);
  not not_8 (not_8_out, S0);
  or or_9 (Carry, eightbitsadder_1_lastcarry, shlshiftright_1_discart, shlshiftleft_1_discart, eightbitssubtrator_1_lastborrow);
  and and_1 (Z, not_1_out, not_2_out, not_3_out, not_4_out, not_5_out, not_6_out, not_7_out, not_8_out);
endmodule

module Key (
  input  ACTIVE,
  input  A,
  output S
);

  and and_1 (S, ACTIVE, A);
endmodule

module Calculator (
  input  A,
  input  B,
  input  C,
  input  A7,
  input  A6,
  input  A5,
  input  A4,
  input  A3,
  input  A2,
  input  A1,
  input  A0,
  input  B7,
  input  B6,
  input  B5,
  input  B4,
  input  B3,
  input  B2,
  input  B1,
  input  B0
);

  wire alu_1_s0, alu_1_s1, alu_1_s2, alu_1_s3, alu_1_s4, alu_1_s5, alu_1_s6, alu_1_s7, decoderhex_1_a,
       decoderhex_1_b, decoderhex_1_c, decoderhex_1_d, decoderhex_1_e, decoderhex_1_f, decoderhex_1_g,
       decoderhex_2_a, decoderhex_2_b, decoderhex_2_c, decoderhex_2_d, decoderhex_2_e, decoderhex_2_f,
       decoderhex_2_g;

  ALU alu_1 (
    .A(A), .B(B), .C(C), .A7(A7), .A6(A6), .A5(A5), .A4(A4), .A3(A3), .A2(A2), .A1(A1), .A0(A0), .B7(B7),
    .B6(B6), .B5(B5), .B4(B4), .B3(B3), .B2(B2), .B1(B1), .B0(B0), .S7(alu_1_s7), .S6(alu_1_s6),
    .S5(alu_1_s5), .S4(alu_1_s4), .S3(alu_1_s3), .S2(alu_1_s2), .S1(alu_1_s1), .S0(alu_1_s0));  // open: Adapter16Bits, Carry, Z
  DecoderHex decoderhex_1 (
    .Ai(alu_1_s7), .Bi(alu_1_s6), .Ci(alu_1_s5), .Di(alu_1_s4), .a(decoderhex_1_a), .b(decoderhex_1_b),
    .c(decoderhex_1_c), .d(decoderhex_1_d), .e(decoderhex_1_e), .f(decoderhex_1_f), .g(decoderhex_1_g));
  DecoderHex decoderhex_2 (
    .Ai(alu_1_s3), .Bi(alu_1_s2), .Ci(alu_1_s1), .Di(alu_1_s0), .a(decoderhex_2_a), .b(decoderhex_2_b),
    .c(decoderhex_2_c), .d(decoderhex_2_d), .e(decoderhex_2_e), .f(decoderhex_2_f), .g(decoderhex_2_g));
  _7_Segment_Display #(.decimalPoint("false")) u_7_segment_display_1 (
    .g(decoderhex_1_g), .f(decoderhex_1_f), .a(decoderhex_1_a), .b(decoderhex_1_b), .e(decoderhex_1_e),
    .d(decoderhex_1_d), .c(decoderhex_1_c));
  _7_Segment_Display #(.decimalPoint("false")) u_7_segment_display_2 (
    .g(decoderhex_2_g), .f(decoderhex_2_f), .a(decoderhex_2_a), .b(decoderhex_2_b), .e(decoderhex_2_e),
    .d(decoderhex_2_d), .c(decoderhex_2_c));
endmodule

module DecoderHex (
  input  Ai,
  input  Bi,
  input  Ci,
  input  Di,
  output a,
  output b,
  output c,
  output d,
  output e,
  output f,
  output g
);

  wire and_1_out, and_2_out, and_3_out, and_4_out, and_5_out, and_6_out, and_7_out, and_8_out, and_9_out,
       and_10_out, and_11_out, and_12_out, and_13_out, and_14_out, and_15_out, and_16_out, and_17_out,
       and_18_out, and_19_out, and_20_out, and_21_out, and_22_out, and_23_out, and_24_out, and_25_out,
       and_26_out, and_27_out, and_28_out, and_29_out, and_30_out, and_31_out, and_32_out, and_33_out,
       and_34_out, and_35_out, and_36_out, and_37_out, and_38_out, and_39_out, and_40_out, and_41_out,
       and_42_out, and_43_out, and_44_out, and_45_out, and_46_out, not_1_out, not_2_out, not_3_out,
       not_4_out, or_1_out, or_2_out, or_3_out, or_4_out, or_5_out, or_6_out, or_7_out, or_8_out, or_9_out,
       or_10_out, or_12_out, or_13_out, or_14_out, or_15_out, or_16_out, or_17_out, or_18_out, or_20_out,
       or_21_out, or_22_out, or_23_out;

  _7_Segment_Display #(.decimalPoint("false")) u_7_segment_display_1 (.g(g), .f(f), .a(a), .b(b), .e(e), .d(d), .c(c));
  not not_1 (not_1_out, Ai);
  not not_2 (not_2_out, Bi);
  not not_3 (not_3_out, Ci);
  not not_4 (not_4_out, Di);
  and and_1 (and_1_out, Ai, not_2_out);
  and and_2 (and_2_out, not_1_out, not_3_out);
  and and_3 (and_3_out, not_1_out, Ci);
  and and_4 (and_4_out, not_1_out, Bi);
  and and_5 (and_5_out, Ai, not_2_out);
  and and_6 (and_6_out, Bi, not_3_out);
  and and_7 (and_7_out, not_1_out, not_2_out);
  and and_8 (and_8_out, not_2_out, not_4_out);
  and and_9 (and_9_out, Ci, not_4_out);
  and and_10 (and_10_out, Ai, Ci);
  and and_11 (and_11_out, Ai, Bi);
  and and_12 (and_12_out, not_1_out, Bi);
  and and_13 (and_13_out, not_2_out, Ci);
  and and_14 (and_14_out, Ai, not_2_out);
  and and_15 (and_15_out, not_1_out, Bi);
  and and_16 (and_16_out, not_2_out, not_4_out);
  and and_17 (and_17_out, not_1_out, Ci);
  and and_18 (and_18_out, not_1_out, Bi);
  and and_19 (and_19_out, and_1_out, not_3_out);
  and and_20 (and_20_out, Ai, not_4_out);
  and and_21 (and_21_out, and_2_out, not_4_out);
  and and_22 (and_22_out, and_3_out, Di);
  and and_23 (and_23_out, Ai, not_3_out);
  or or_1 (or_1_out, and_4_out, and_5_out);
  and and_24 (and_24_out, not_3_out, Di);
  and and_25 (and_25_out, not_2_out, not_3_out);
  and and_26 (and_26_out, not_2_out, Di);
  and and_27 (and_27_out, and_6_out, Di);
  and and_28 (and_28_out, and_7_out, not_4_out);
  and and_29 (and_29_out, not_2_out, Ci);
  and and_30 (and_30_out, Bi, Ci);
  or or_2 (or_2_out, and_8_out, and_9_out);
  or or_3 (or_3_out, and_10_out, and_11_out);
  and and_31 (and_31_out, not_3_out, not_4_out);
  and and_32 (and_32_out, and_12_out, not_3_out);
  or or_4 (or_4_out, and_13_out, and_14_out);
  and and_33 (and_33_out, and_15_out, not_3_out);
  and and_34 (and_34_out, Ci, not_4_out);
  and and_35 (and_35_out, Ai, Di);
  or or_5 (or_5_out, and_16_out, and_17_out);
  and and_36 (and_36_out, and_18_out, Di);
  or or_6 (or_6_out, and_19_out, and_20_out);
  and and_37 (and_37_out, Bi, Ci);
  or or_7 (or_7_out, and_21_out, and_22_out);
  and and_38 (and_38_out, not_2_out, not_4_out);
  and and_39 (and_39_out, and_23_out, Di);
  and and_40 (and_40_out, not_1_out, not_2_out);
  or or_8 (or_8_out, or_1_out, and_24_out);
  or or_9 (or_9_out, and_25_out, and_26_out);
  or or_10 (or_10_out, and_27_out, and_28_out);
  and and_41 (and_41_out, and_29_out, Di);
  and and_42 (and_42_out, Ai, not_3_out);
  and and_43 (and_43_out, and_30_out, not_4_out);
  or or_11 (e, or_2_out, or_3_out);
  or or_12 (or_12_out, and_31_out, and_32_out);
  and and_44 (and_44_out, Bi, not_4_out);
  and and_45 (and_45_out, Ai, not_2_out);
  and and_46 (and_46_out, Ai, Ci);
  or or_13 (or_13_out, or_4_out, and_33_out);
  or or_14 (or_14_out, and_34_out, and_35_out);
  or or_15 (or_15_out, or_5_out, and_36_out);
  or or_16 (or_16_out, or_6_out, and_37_out);
  or or_17 (or_17_out, or_7_out, and_38_out);
  or or_18 (or_18_out, and_39_out, and_40_out);
  or or_19 (c, or_8_out, or_9_out);
  or or_20 (or_20_out, or_10_out, and_41_out);
  or or_21 (or_21_out, and_42_out, and_43_out);
  or or_22 (or_22_out, or_12_out, and_44_out);
  or or_23 (or_23_out, and_45_out, and_46_out);
  or or_24 (g, or_13_out, or_14_out);
  or or_25 (a, or_15_out, or_16_out);
  or or_26 (b, or_17_out, or_18_out);
  or or_27 (d, or_20_out, or_21_out);
  or or_28 (f, or_22_out, or_23_out);
endmodule

module ALU16BITS (
  input  A15,
  input  A14,
  input  A13,
  input  A12,
  input  A11,
  input  A10,
  input  A9,
  input  A8,
  input  A7,
  input  A6,
  input  A5,
  input  A4,
  input  A3,
  input  A2,
  input  A1,
  input  A0,
  input  B15,
  input  B14,
  input  B13,
  input  B12,
  input  B11,
  input  B10,
  input  B9,
  input  B8,
  input  B7,
  input  B6,
  input  B5,
  input  B4,
  input  B3,
  input  B2,
  input  B1,
  input  B0,
  input  A,
  input  B,
  input  C,
  output S15,
  output S14,
  output S13,
  output S12,
  output S11,
  output S10,
  output S9,
  output S8,
  output S7,
  output S6,
  output S5,
  output S4,
  output S3,
  output S2,
  output S1,
  output S0,
  output Z
);

  wire alu_1_carry, alu_1_z, alu_2_carry, alu_2_z;

  ALU alu_1 (
    .A(A), .B(B), .C(C), .A7(A15), .A6(A14), .A5(A13), .A4(A12), .A3(A11), .A2(A10), .A1(A9), .A0(A8),
    .B7(B15), .B6(B14), .B5(B13), .B4(B12), .B3(B11), .B2(B10), .B1(B9), .B0(B8),
    .Adapter16Bits(alu_2_carry), .S7(S15), .S6(S14), .S5(S13), .S4(S12), .S3(S11), .S2(S10), .S1(S9),
    .S0(S8), .Carry(alu_1_carry), .Z(alu_1_z));
  ALU alu_2 (
    .A(A), .B(B), .C(C), .A7(A7), .A6(A6), .A5(A5), .A4(A4), .A3(A3), .A2(A2), .A1(A1), .A0(A0), .B7(B7),
    .B6(B6), .B5(B5), .B4(B4), .B3(B3), .B2(B2), .B1(B1), .B0(B0), .Adapter16Bits(alu_1_carry), .S7(S7),
    .S6(S6), .S5(S5), .S4(S4), .S3(S3), .S2(S2), .S1(S1), .S0(S0), .Carry(alu_2_carry), .Z(alu_2_z));
  and and_1 (Z, alu_1_z, alu_2_z);
endmodule
